# Fritzing sketch System_Design (saved by Fritzing 0.9.3b)

parts:
  U1 = ESP32-38PinWide [part_number=ESP32-38PinWide]
  ESP32_-_Back1 = ESP32 - CAM
  PWM1 = PCA9685 16x12-bit PWM Breakout
  J1 = Basic Servo
  DFRobot_DFPlayer_Mini1 = DFRobot DFPlayer Mini [part_number=DFR0299]
  Mod1 = 3S-BMS
  Linh_kiện1 = Lithium Ion Cylindrical Battery 3.7v 2200mAh [part_number=1781]
  Linh_kiện2 = VERTER 5V USB Buck-Boost
  Power_plug1 = Power plug
  SPKR1 = Loudspeaker
  J2 = Piezo Speaker
  R1 = Resistor [tolerance=±5% resistance=220 package=THT]
  Linh_kiện3 = Arduino Nano (Rev3.0) (ICSP)
  LCD2004-I2C1 = LCD2004-I2C
  hc-sr1 = hc-sr04
  M1 = DC Motor
  A1 = X804
  YL-83_-_Detection_Board1 = YL-83 Rain Sensor - Detection Board  # not connected
  Mod2 = KY-025 Reed Switch Module [package="Breakout board"]
  Linh_kiện4 = Soil Moisture Sensor
  F1 = Fan - Ventilador [package=THT]
  J3 = Peltier Element  # not connected
  Linh_kiện7 = 24 NeoPixel Ring [part_number=1586]
  U2 = LM2596 step down module
  Linh_kiện8 = Lithium Ion Cylindrical Battery 3.7v 2200mAh [part_number=1781]
  Linh_kiện9 = Lithium Ion Cylindrical Battery 3.7v 2200mAh [part_number=1781]
  S1 = Toggle Switch [package=THT]
  Mod3 = Solar Charge Controller [part_number="KLD Series Solar Charge Controller PWM" package=PWM-Model]
  S2 = Toggle Switch [package=THT]
  S3 = Toggle Switch [package=THT]
  Part1 = Solar Panel [package="Renogy 50 Watts 12 Volt Monocrystalline Bendable Solar Panel"]
  Linh_kiện10 = BH1750
  DHT1 = DHT11 Humitidy and Temperature Sensor
  U3 = LM2596 step down module
  U4 = LM2596 step down module
  KY-1 = Keyes Relay [package=THT]
  S4 = Limit Switch [package="Breakout Board"]
  KY-2 = Keyes Relay [package=THT]
  KY-3 = Keyes Relay [package=THT]
  S5 = Limit Switch [package="Breakout Board"]
  M2 = DC Motor
  R2 = Resistor [tolerance=±5% resistance=220 package=THT]
  J4 = Basic Servo
  J5 = Basic Servo

nets:
  N1: U1.GPIO32, KY-2.signal
  N2: U1.GPIO33, KY-1.signal
  N3: U1.GPIO25, Linh_kiện7.IN
  N4: U1.GPIO26, S5.S
  N5: U1.GPIO27, S4.S
  N6: U1.GPIO14, Linh_kiện4.SIG
  GND: U1.GND, ESP32_-_Back1.GND, PWM1.no_name_yet#601, PWM1.no_name_yet#701, PWM1.no_name_yet#1004, Linh_kiện2.GND, Power_plug1.GND, J2.pin1, Linh_kiện3.GND, A1.Pin_1, A1.Pin_4, A1.Pin_5, Mod2.G, Linh_kiện4.GND, Linh_kiện7.GND, U2.IN-, U2.OUT-, Mod3.Connector_6, DHT1.GND, U3.IN-, U3.OUT-, U4.IN-, U4.OUT-, KY-1.ground, KY-2.ground, KY-3.ground, M2.pin_1, J5.gnd
  N7: U1.GPIO13, ESP32_-_Back1.GPIO4
  VIN: U1.VIN, ESP32_-_Back1.5V, Linh_kiện3.VIN, U2.OUT+
  N8: U1.GPIO15, Mod2.D0
  N9: U1.GPIO2, KY-3.signal
  N10: U1.GPIO4, ESP32_-_Back1.GPIO13
  N11: U1.GPIO16, Linh_kiện3.D2
  N12: U1.GPIO17, Linh_kiện3.D3
  N13: U1.GPIO5, DHT1.DATA
  N14: U1.GPIO18, hc-sr1.Echo
  N15: U1.GPIO19, hc-sr1.Trig
  N16: U1.GPIO21, PWM1.no_name_yet#604, Linh_kiện10.SDA
  N17: U1.GPIO22, PWM1.no_name_yet#603, Linh_kiện10.SCL
  N18: U1.GPIO23, J2.pin2
  N19: PWM1.no_name_yet#0, J5.pulse
  N20: PWM1.no_name_yet#1, J4.pulse
  N21: PWM1.no_name_yet#2, J1.pulse
  VDD: PWM1.no_name_yet#104, PWM1.no_name_yet#706, Linh_kiện7.VDD, U4.OUT+, KY-1.power, KY-2.power, J5.vcc
  N22: PWM1.no_name_yet#605, KY-3.power
  VCC: DFRobot_DFPlayer_Mini1.VCC, LCD2004-I2C1.VCC, hc-sr1.VCC, Mod2.+, Linh_kiện4.VCC, Linh_kiện10.VCC, DHT1.VDD, U3.OUT+, S4.V, S5.V
  N23: DFRobot_DFPlayer_Mini1.RX, R1.Pin_0
  N24: DFRobot_DFPlayer_Mini1.TX, R2.Pin_0
  N25: DFRobot_DFPlayer_Mini1.SPK_1, SPKR1.pin2
  GND_2: DFRobot_DFPlayer_Mini1.GND-1, DFRobot_DFPlayer_Mini1.GND-2, LCD2004-I2C1.GND, hc-sr1.GND, Linh_kiện10.GND, S4.G, S5.G
  N26: DFRobot_DFPlayer_Mini1.SPK_2, SPKR1.pin1
  N27: Mod1.0V, Linh_kiện1.negative
  N28: Mod1.4.2V, Linh_kiện1.positive, Linh_kiện8.negative
  N29: Mod1.8.4V, Linh_kiện8.positive, Linh_kiện9.negative
  N30: Mod1.-, Mod3.Connector_4
  N31: Mod1.+, S1.COM
  N32: Mod1.12.6V, Linh_kiện9.positive
  N33: Linh_kiện2.VIN, U2.IN+, S3.COM, U3.IN+, U4.IN+, KY-1.C, KY-2.C, KY-3.C
  N34: Power_plug1.VCC, A1.Pin_3
  N35: R1.Pin_1, Linh_kiện3.D10
  N36: Linh_kiện3.D11/MOSI, R2.Pin_1
  N37: Linh_kiện3.A5, LCD2004-I2C1.SCL
  N38: Linh_kiện3.A4, LCD2004-I2C1.SDA
  N39: M1.pin_2, KY-2.NO
  N40: A1.Pin_2, Mod3.Connector_5
  N41: A1.Pin_6, S3.L1
  N42: F1.5V, KY-1.NO
  N43: S1.L1, Mod3.Connector_3
  N44: Mod3.Connector_1, S2.L1
  N45: Mod3.Connector_2, Part1.Connector_2
  N46: S2.COM, Part1.Connector_1
  N47: KY-3.NO, M2.pin_2

custom parts:
  ESP32-38PinWide: Generic 38-Pin ESP32 with wide format (only access to one side of pins on a breadboard) based on Stephen Lilley's HiLetgo ESP-WROOM-32 ESP32 ESP-32S Development Board.
  ESP32 - CAM: The ESP32-CAM has a very competitive small-size camera module that can operate independently as a minimum system with a footprint of only 27*40.5*4.5mm and a deep sleep current of up to 6mA.
  3S-BMS: 3S-BMS LIPO battery charger / protection unit. Note pcb does not match the board as it will likely connect with wires, so pcb is 6 pads suitable for .1in header pins.
  Lithium Ion Cylindrical Battery 3.7v 2200mAh: This lithium ion battery has a capacity of 2200mAh and a protection circuit that provides over-voltage, under-voltage and over-current protection. This cell can provide 2C of peak current (4400mA). Note that these batteries are not designed to sustain such high loads, we suggest keeping any constant current draw under about 0.5C (1 Amp).
  VERTER 5V USB Buck-Boost: VERTER can take battery voltages from 3-12VDC and output a nice 5V DC, which makes it a perfect universal power supply for your portable project! Where Verter really shines is when you have a battery or power range that can fluctuate a lot, or you don't know what you'll end up using.
  LCD2004-I2C: A standard character display with 4x20 characters. Comes in many colors with LCM2004 IIC attached.
  X804: This is a power outage automatic switch module for 12V-48V battery.
  YL-83 Rain Sensor - Detection Board: The YL-83 is a rain sensor that has more resistance when dry and less resistance when wet. The module runs at 5V.
  KY-025 Reed Switch Module: KY-025 Reed Switch Module, it reacts in the presence of a magnetic field.
  Fan - Ventilador: Ventilador de 2 pines, se encuentra comunmente en computadoras de escritorio
  24 NeoPixel Ring: 24 ultra bright smart LED NeoPixels are arranged in a circle with 2.6" (66mm) outer diameter. The rings are 'chainable' - connect the output pin of one to the input pin of another. Use only one microcontroller pin to control as many as you can chain together! Each LED is addressable as the driver chip is inside the LED. Each one has ~18mA constant current drive so the color will be very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
  LM2596 step down module: LM2596 DC-DC step down power supply module 3 A.
  Solar Charge Controller: PWM-Solar Charge Controller
  Solar Panel: Renogy 50 Watts 12 Volt Solar Panel
  BH1750: Light Sensor
  DHT11 Humitidy and Temperature Sensor: DHT11 Humidity and Temperature Sensor
  Keyes Relay: The Keyes 5V relay module is suitable for SCM development, home appliance control. It uses a 5V~12V TIL control signal which can control DC / AC signal.
  Limit Switch: Generic limit switch commonly found on 3D printers. Typical lever microswitch mounted on a PCB board with a 3 pin JST XH connector.
